// Logisim project angles.circ as structural Verilog: 6 circuits, main circuit main
module main (
  input  _1,
  input  _2,
  input  _3,
  input  _4,
  input  [1:0] _5__tile_type,
  input  _6,
  input  _7,
  input  _8,
  input  _9
);

  wire image_1, image_1s, image_2, image_3, image_3s, image_4, image_6, image_7, image_7s, image_8, image_9,
       image_9s;
  wire [15:0] angle_processor_1_tile_matrix;

  // Probe on {image_1, image_1s, image_2, image_3, image_3s, image_4, image_6, image_7, image_7s, image_8, image_9, image_9s}
  angle_processor angle_processor_1 (
    ._1(_1), ._2(_2), ._3(_3), ._4(_4), ._5__tile_type(_5__tile_type), ._6(_6), ._7(_7), ._8(_8), ._9(_9),
    .tile_matrix(angle_processor_1_tile_matrix),
    .tile_images_used({image_1, image_1s, image_2, image_3, image_3s, image_4, image_6, image_7, image_7s, image_8, image_9, image_9s}));
  // Probe on angle_processor_1_tile_matrix
  LED led_1 (.in(image_1));
  LED led_2 (.in(image_1s));
  LED led_3 (.in(image_4));
  LED led_4 (.in(image_7));
  LED led_5 (.in(image_7s));
  DotMatrix #(.inputtype("row"), .matrixcols(4), .matrixrows(4)) dotmatrix_1 (
    .row0(angle_processor_1_tile_matrix[15:12]), .row1(angle_processor_1_tile_matrix[11:8]),
    .row2(angle_processor_1_tile_matrix[7:4]), .row3(angle_processor_1_tile_matrix[3:0]));
  DotMatrix #(.inputtype("row"), .matrixcols(4), .matrixrows(4)) dotmatrix_2 (
    .row0(angle_processor_1_tile_matrix[15:12]), .row1(angle_processor_1_tile_matrix[11:8]),
    .row2(angle_processor_1_tile_matrix[7:4]), .row3(angle_processor_1_tile_matrix[3:0]));
  LED led_6 (.in(image_2));
  LED led_7 (.in(image_8));
  LED led_8 (.in(image_3));
  LED led_9 (.in(image_3s));
  LED led_10 (.in(image_6));
  LED led_11 (.in(image_9));
  LED led_12 (.in(image_9s));

  // Notes on the sheet:
  //   Road / Water Angles
  //   Pin 5: tile type (has no effect)
  //   Other pins: 0 for water / road, 1 for other tiles
  //   tile image picker
  //   road
  //   water
endmodule

module angle_processor (
  input  _1,
  input  _2,
  input  _3,
  input  _4,
  input  [1:0] _5__tile_type,
  input  _6,
  input  _7,
  input  _8,
  input  _9,
  output [15:0] tile_matrix,
  output [11:0] tile_images_used
);

  rows_1__4 rows_1_4_1 (
    .horizontal(_2), .W_edge(_4), .E_edge(_6), .W_corner(_1), .E_corner(_3), .out_row(tile_matrix[15:12]));
  rows_2__3 rows_2_3_1 (.W_edge(_4), .E_edge(_6), .out_row(tile_matrix[11:8]));
  rows_1__4 rows_1_4_2 (
    .horizontal(_8), .W_edge(_4), .E_edge(_6), .W_corner(_7), .E_corner(_9), .out_row(tile_matrix[3:0]));
  LED led_1 (.in(tile_images_used[11]));
  LED led_2 (.in(tile_images_used[10]));
  LED led_3 (.in(tile_images_used[6]));
  LED led_4 (.in(tile_images_used[4]));
  LED led_5 (.in(tile_images_used[3]));
  DotMatrix #(.inputtype("row"), .matrixcols(4), .matrixrows(4)) dotmatrix_1 (
    .row0(tile_matrix[15:12]), .row1(tile_matrix[11:8]), .row2(tile_matrix[11:8]), .row3(tile_matrix[3:0]));
  DotMatrix #(.inputtype("row"), .matrixcols(4), .matrixrows(4)) dotmatrix_2 (
    .row0(tile_matrix[15:12]), .row1(tile_matrix[11:8]), .row2(tile_matrix[11:8]), .row3(tile_matrix[3:0]));
  corner_image_picker corner_image_picker_1 (
    .Corner(_1), .Edge_1(_2), .Edge_2(_4), .corner_out__corner___edges(tile_images_used[11]),
    .corner_out__corner_only(tile_images_used[10]));
  edge_image_picker edge_image_picker_1 (
    .Edge(_4), .Corner_1_image_picked(tile_images_used[11]), .Corner_2_image_picked(tile_images_used[4]),
    .Pick_edge_image(tile_images_used[6]));
  corner_image_picker corner_image_picker_2 (
    .Corner(_7), .Edge_1(_4), .Edge_2(_8), .corner_out__corner___edges(tile_images_used[4]),
    .corner_out__corner_only(tile_images_used[3]));
  LED led_6 (.in(tile_images_used[9]));
  LED led_7 (.in(tile_images_used[2]));
  LED led_8 (.in(tile_images_used[8]));
  LED led_9 (.in(tile_images_used[7]));
  LED led_10 (.in(tile_images_used[5]));
  LED led_11 (.in(tile_images_used[1]));
  LED led_12 (.in(tile_images_used[0]));
  edge_image_picker edge_image_picker_2 (
    .Edge(_2), .Corner_1_image_picked(tile_images_used[11]), .Corner_2_image_picked(tile_images_used[8]),
    .Pick_edge_image(tile_images_used[9]));
  edge_image_picker edge_image_picker_3 (
    .Edge(_8), .Corner_1_image_picked(tile_images_used[4]), .Corner_2_image_picked(tile_images_used[1]),
    .Pick_edge_image(tile_images_used[2]));
  corner_image_picker corner_image_picker_3 (
    .Corner(_3), .Edge_1(_2), .Edge_2(_6), .corner_out__corner___edges(tile_images_used[8]),
    .corner_out__corner_only(tile_images_used[7]));
  edge_image_picker edge_image_picker_4 (
    .Edge(_6), .Corner_1_image_picked(tile_images_used[8]), .Corner_2_image_picked(tile_images_used[1]),
    .Pick_edge_image(tile_images_used[5]));
  corner_image_picker corner_image_picker_4 (
    .Corner(_9), .Edge_1(_6), .Edge_2(_8), .corner_out__corner___edges(tile_images_used[1]),
    .corner_out__corner_only(tile_images_used[0]));

  assign tile_matrix[7:4] = tile_matrix[11:8];

  // Other names for the same wires on the sheet: _5[1:0] = _5__tile_type; E_edge = _6; N_edge = _2; NE = _3; NW = _1;
  //   S_edge = _8; SE = _9; SW = _7; image_9s = tile_images_used[0]; image_9 = tile_images_used[1];
  //   image_8 = tile_images_used[2]; image_7s = tile_images_used[3]; image_7 = tile_images_used[4];
  //   image_6 = tile_images_used[5]; image_4 = tile_images_used[6]; image_3s = tile_images_used[7];
  //   image_3 = tile_images_used[8]; image_2 = tile_images_used[9]; image_1s = tile_images_used[10];
  //   image_1 = tile_images_used[11]; Row_4[3:0] = tile_matrix[3:0]; Rows_2__3[3:0] = tile_matrix[11:8];
  //   Row_1[3:0] = tile_matrix[15:12]; W_edge = _4

  // Notes on the sheet:
  //   Inputs
  //   Edges
  //   Corners
  //   tile matrix processor
  //   tile preview (road)
  //   tile preview (water)
  //   tile images
  //   tile image picker
endmodule

module rows_1__4 (
  input  horizontal,
  input  W_edge,
  input  E_edge,
  input  W_corner,
  input  E_corner,
  output [3:0] out_row
);

  wire NE_SE_out, NW_SW_out;

  or NW_SW (NW_SW_out, horizontal, W_edge);
  or NE_SE (NE_SE_out, horizontal, E_edge);
  assign out_row[2:1] = {{1{horizontal}}, horizontal};  // Bit_Extender bit_extender_1
  Multiplexer #(.enable("false")) multiplexer_1 (.in0(W_corner), .in1(NW_SW_out), .out(out_row[3]), .sel(NW_SW_out));
  Multiplexer #(.enable("false")) multiplexer_2 (.in0(E_corner), .in1(NE_SE_out), .out(out_row[0]), .sel(NE_SE_out));
endmodule

module rows_2__3 (
  input  W_edge,
  input  E_edge,
  output [3:0] out_row
);


  assign out_row = {W_edge, 2'b00, E_edge};
endmodule

module corner_image_picker (
  input  Corner,
  input  Edge_1,
  input  Edge_2,
  output corner_out__corner___edges,
  output corner_out__corner_only
);

  wire nor_1_out;

  Multiplexer #(.enable("false")) multiplexer_1 (
    .in0(1'b0), .in1(Corner), .out(corner_out__corner_only), .sel(nor_1_out));
  nor nor_1 (nor_1_out, Edge_1, Edge_2);
  and and_1 (corner_out__corner___edges, Edge_1, Edge_2);
endmodule

module edge_image_picker (
  input  Edge,
  input  Corner_1_image_picked,
  input  Corner_2_image_picked,
  output Pick_edge_image
);

  Multiplexer #(.select(2), .enable("false")) multiplexer_1 (
    .in0(Edge), .in1(1'b1), .in2(1'b1), .in3(1'b0), .out(Pick_edge_image),
    .sel({Corner_2_image_picked, Corner_1_image_picked}));
endmodule
